// Digital circuit Control_Unit.dig as structural Verilog
module Control_Unit (
  input  x1,
  input  x0,
  input  CLOCK,
  output y1,
  output y0
);

  wire and_1_out, and_2_out, and_3_out, and_4_out, or_1_out, or_2_out, z1_nq;

  and and_1 (and_1_out, ~x1, y0);  // And
  and and_2 (and_2_out, y0, x0);
  and and_3 (and_3_out, z1_nq, ~x0);  // And
  or or_1 (or_1_out, ~x1, x0);  // Or
  or or_2 (or_2_out, and_1_out, and_2_out);
  and and_4 (and_4_out, and_3_out, x1);
  JK_FF z1 (.J(or_2_out), .C(CLOCK), .K(y1), .Q(y1), .nQ(z1_nq));
  JK_FF z0 (.J(and_4_out), .C(CLOCK), .K(or_1_out), .Q(y0));  // open: nQ
endmodule
